// Logisim project curcuit.circ as structural Verilog
module main (
);

  wire clck, clock_1_out, decoder_1_out1, dipswitch_1_sw1, HLT, not_1_out, reset;
  wire [2:0] cpu_1_odd;
  wire [23:0] bit_extender_1_out;
  wire [31:0] cpu_1_od1, cpu_1_od2;

  and and_1 (clck, clock_1_out, not_1_out);
  not not_1 (not_1_out, dipswitch_1_sw1);
  Clock clock_1 (.out(clock_1_out));
  DipSwitch #(.number(2)) dipswitch_1 (.sw1(dipswitch_1_sw1), .sw2(HLT));
  Button R (.out(reset));
  blank blank_1 ();
  CPU cpu_1 (.HLT(HLT), .reset(reset), .Clock(clck), .OD1(cpu_1_od1), .OD2(cpu_1_od2), .ODD(cpu_1_odd));
  Decoder #(.enable("false"), .select(3)) decoder_1 (
    .out1(decoder_1_out1), .sel(cpu_1_odd));  // open: out0, out2, out3, out4, out5, out6, out7
  Bit_Extender #(.in_width(32), .out_width(24)) bit_extender_1 (.in(cpu_1_od2), .out(bit_extender_1_out));
  // RGB_Video #(.height(256), .scale(1), .width(256)) rgb_video_1: pin names not known; wires that end beside it: reset, clck, decoder_1_out1, cpu_1_od1[7:0], cpu_1_od1[15:8], bit_extender_1_out
endmodule

module ProgramCounter (
  input  [31:0] JmpAddr,
  input  Reset,
  input  Jmp,
  input  Clock,
  output [31:0] ip
);

  wire [31:0] adder_1_out, multiplexer_1_out;

  Adder #(.width(32)) adder_1 (.a(ip), .b(32'h1), .out(adder_1_out));  // open: cin, cout
  Multiplexer #(.width(32)) multiplexer_1 (.in0(adder_1_out), .in1(JmpAddr), .out(multiplexer_1_out), .sel(Jmp));
  Register #(.width(32)) PC (.D(multiplexer_1_out), .en(1'b1), .Q(ip), .clk(Clock), .clr(Reset));
endmodule

module CPU (
  input  reset,
  input  Clock,
  input  HLT,
  output [2:0] ODD,
  output [31:0] OD1,
  output [31:0] OD2
);

  wire ALU_Calc, and_2_out, and_3_out, and_4_out, ARI, Button_1_out, clck, DRW, IRAO, IRI, IRO, JMP, MI, ML,
       MO, OD1W, OD2W, ODW, OEn, or_2_out, PCO, PCUp, reset_t, SR1O, SR2O;
  wire [2:0] ALU_1_co, flags, ODD_t;
  wire [3:0] ALU_OP, DRID, InstrDecoder_1_op, SR1ID, SR2ID;
  wire [23:0] adr_bus, PC_q, register_1_q;
  wire [31:0] ALU_1_a_o, bit_extender_1_out, controlled_buffer_7_out, data_bus, IR_q, RAM_1_dout, SR1, SR2;

  Button Button_1 (.out(Button_1_out));
  or or_1 (reset_t, Button_1_out, reset);
  or or_2 (or_2_out, HLT, HLT);
  Register #(.width(24)) register_1 (.D(adr_bus), .en(ARI), .clk(clck), .Q(register_1_q), .clr(reset_t));
  RAM #(.addrWidth(24), .dataWidth(32)) RAM_1 (
    .addr(adr_bus), .we(MI), .oe(ML), .clk(clck), .din(data_bus), .dout(RAM_1_dout));
  Register #(.width(32)) IR (.D(data_bus), .en(IRI), .clk(clck), .Q(IR_q), .clr(reset_t));
  and and_1 (clck, Clock, ~or_2_out);  // AND_Gate
  assign adr_bus = PCO ? PC_q : 24'bz;  // Controlled_Buffer controlled_buffer_1
  Counter #(.max('hffffff), .ongoal("continue"), .width(24)) PC (
    .load(JMP), .D(register_1_q), .count(PCUp), .Q(PC_q), .up(1'b1), .clk(PCUp), .clr(reset_t));  // open: carry
  assign bit_extender_1_out = {{8{1'b0}}, IR_q[23:0]};  // Bit_Extender bit_extender_1
  assign data_bus = IRO ? bit_extender_1_out : 32'bz;  // Controlled_Buffer controlled_buffer_2
  assign adr_bus = IRAO ? IR_q[23:0] : 24'bz;  // Controlled_Buffer controlled_buffer_3
  assign data_bus = MO ? RAM_1_dout : 32'bz;  // Controlled_Buffer controlled_buffer_4
  ALU ALU_1 (
    .C_or_B(1'b0), .Op(ALU_OP), .N1(SR1), .N2(SR2), .MC({32{1'b0}}), .CO(ALU_1_co[0]), .BO(ALU_1_co[1]),
    .A_O(ALU_1_a_o), .Comp(ALU_1_co[2]));  // open: MCO
  assign data_bus = ALU_Calc ? ALU_1_a_o : 32'bz;  // Controlled_Buffer controlled_buffer_5
  Register #(.width(3)) u_Flags (.D(ALU_1_co), .en(ALU_Calc), .clk(clck), .Q(flags), .clr(reset_t));
  InstrDecoder InstrDecoder_1 (
    .IR(IR_q), .flags(flags), .ALUOP(ALU_OP), .DR(DRID), .SR2(SR2ID), .SR1(SR1ID), .DDI(ODW), .OD1I(OD1W),
    .OD2I(OD2W), .ODD(ODD_t), .OP(InstrDecoder_1_op));
  RegisterBank RegisterBank_1 (
    .C(clck), .R(reset_t), .W(DRW), .RS1(SR1ID), .RS2(SR2ID), .DR(DRID), .DRD(data_bus), .S1(SR1), .S2(SR2));
  assign data_bus = SR1O ? SR1 : 32'bz;  // Controlled_Buffer controlled_buffer_6
  assign controlled_buffer_7_out = SR2O ? SR2 : 32'bz;  // Controlled_Buffer controlled_buffer_7
  Hex_Digit_Display #(.decimalPoint("false")) Hex_Digit_Display_1 (.value(InstrDecoder_1_op));
  Bit_Extender #(.in_width(32), .out_width(24)) bit_extender_2 (.in(controlled_buffer_7_out), .out(adr_bus));
  and and_2 (and_2_out, ODW, OEn);
  and and_3 (and_3_out, OD1W, OEn);
  and and_4 (and_4_out, OD2W, OEn);
  Executor Executor_1 (
    .OP(InstrDecoder_1_op), .clock(clck), .reset(reset_t), .JMP(JMP), .PCU(PCUp), .PCO(PCO), .DRW(DRW),
    .SR1O(SR1O), .SR2O(SR2O), .ALUCalc(ALU_Calc), .MI(MI), .ML(ML), .MO(MO), .IRI(IRI), .IRO(IRO),
    .IRAO(IRAO), .ARI(ARI), .OEn(OEn));  // open: HLT
  Register #(.width(3)) register_2 (.D(ODD_t), .en(and_2_out), .clk(clck), .Q(ODD), .clr(reset_t));
  Register #(.width(32)) register_3 (.D(data_bus), .en(and_3_out), .clk(clck), .Q(OD1), .clr(reset_t));
  Register #(.width(32)) register_4 (.D(data_bus), .en(and_4_out), .clk(clck), .Q(OD2), .clr(reset_t));
endmodule

module ALU (
  input  C_or_B,
  input  [3:0] Op,
  input  [31:0] N1,
  input  [31:0] N2,
  input  [31:0] MC,
  output CO,
  output BO,
  output [31:0] MCO,
  output [31:0] A_O,
  output Comp
);

  wire comparator_1_eq, comparator_1_gt, comparator_1_lt, or_2_out, or_3_out;
  wire [4:0] bit_extender_1_out, bit_extender_2_out, bit_extender_3_out, bit_extender_4_out,
       bit_extender_5_out;
  wire [31:0] adder_1_out, and_1_out, multiplier_1_out, nand_1_out, negator_1_out, not_1_out, or_1_out,
       shifter_1_out, shifter_2_out, shifter_3_out, shifter_4_out, shifter_5_out, subtractor_1_out,
       xnor_1_out, xor_1_out;

  Bit_Extender #(.in_width(32), .out_width(5), .\type ("zero")) bit_extender_1 (.in(N2), .out(bit_extender_1_out));
  Bit_Extender #(.in_width(32), .out_width(5), .\type ("zero")) bit_extender_2 (.in(N2), .out(bit_extender_2_out));
  Bit_Extender #(.in_width(32), .out_width(5), .\type ("zero")) bit_extender_3 (.in(N2), .out(bit_extender_3_out));
  Bit_Extender #(.in_width(32), .out_width(5), .\type ("zero")) bit_extender_4 (.in(N2), .out(bit_extender_4_out));
  Bit_Extender #(.in_width(32), .out_width(5), .\type ("zero")) bit_extender_5 (.in(N2), .out(bit_extender_5_out));
  Adder #(.width(32)) adder_1 (.a(N1), .b(N2), .out(adder_1_out), .cin(C_or_B), .cout(CO));
  Subtractor #(.width(32)) subtractor_1 (.a(N1), .b(N2), .out(subtractor_1_out), .bin(C_or_B), .bout(BO));
  Multiplier #(.width(32)) multiplier_1 (.a(N1), .b(N2), .out(multiplier_1_out), .cin(MC), .cout(MCO));
  Negator #(.width(32)) negator_1 (.in(N1), .out(negator_1_out));
  assign and_1_out = N1 & N2;  // AND_Gate and_1, 32 bits wide
  assign or_1_out = N1 | N2;  // OR_Gate or_1, 32 bits wide
  assign not_1_out = ~N1;  // NOT_Gate not_1, 32 bits wide
  assign nand_1_out = ~(N1 & N2);  // NAND_Gate nand_1, 32 bits wide
  assign xor_1_out = N1 ^ N2;  // XOR_Gate xor_1, 32 bits wide
  assign xnor_1_out = ~(N1 ^ N2);  // XNOR_Gate xnor_1, 32 bits wide
  Shifter #(.width(32)) shifter_1 (.in(N1), .\dist (bit_extender_1_out), .out(shifter_1_out));
  Shifter #(.shift("lr"), .width(32)) shifter_2 (.in(N1), .\dist (bit_extender_2_out), .out(shifter_2_out));
  Shifter #(.shift("ar"), .width(32)) shifter_3 (.in(N1), .\dist (bit_extender_3_out), .out(shifter_3_out));
  Shifter #(.shift("rl"), .width(32)) shifter_4 (.in(N1), .\dist (bit_extender_4_out), .out(shifter_4_out));
  Shifter #(.shift("rr"), .width(32)) shifter_5 (.in(N1), .\dist (bit_extender_5_out), .out(shifter_5_out));
  Comparator #(.mode("unsigned"), .width(32)) comparator_1 (
    .a(N1), .b(N2), .gt(comparator_1_gt), .eq(comparator_1_eq), .lt(comparator_1_lt));
  or or_2 (or_2_out, comparator_1_gt, comparator_1_eq);
  or or_3 (or_3_out, comparator_1_eq, comparator_1_lt);
  Multiplexer #(.select(4), .width(32)) multiplexer_1 (
    .in0(adder_1_out), .in1(subtractor_1_out), .in2(multiplier_1_out), .in3(negator_1_out), .in4(and_1_out),
    .in5(or_1_out), .in6(not_1_out), .in7(nand_1_out), .in8(xor_1_out), .in9(xnor_1_out),
    .in10(shifter_1_out), .in11(shifter_2_out), .in12(shifter_3_out), .in13(shifter_4_out),
    .in14(shifter_5_out), .in15({32{1'b0}}), .out(A_O), .sel(Op));
  Multiplexer #(.select(4)) multiplexer_2 (
    .in0(comparator_1_gt), .in1(comparator_1_eq), .in2(comparator_1_lt), .in3(or_2_out), .in4(or_3_out),
    .in5(1'b0), .in6(1'b0), .in7(1'b0), .in8(1'b0), .in9(1'b0), .in10(1'b0), .in11(1'b0), .in12(1'b0),
    .in13(1'b0), .in14(1'b0), .in15(1'b0), .out(Comp), .sel(Op));
endmodule

module RegisterBank (
  input  C,
  input  R,
  input  W,
  input  [3:0] RS1,
  input  [3:0] RS2,
  input  [3:0] DR,
  input  [31:0] DRD,
  output [31:0] S1,
  output [31:0] S2
);

  wire and_1_out, and_2_out, and_3_out, and_4_out, and_5_out, and_6_out, and_7_out, and_8_out, and_9_out,
       and_10_out, and_11_out, and_12_out, and_13_out, and_14_out, and_15_out, and_16_out, decoder_1_out0,
       decoder_1_out1, decoder_1_out2, decoder_1_out3, decoder_1_out4, decoder_1_out5, decoder_1_out6,
       decoder_1_out7, decoder_1_out8, decoder_1_out9, decoder_1_out10, decoder_1_out11, decoder_1_out12,
       decoder_1_out13, decoder_1_out14, decoder_1_out15;
  wire [31:0] R0_q, R1_q, R2_q, R3_q, R4_q, R5_q, R6_q, R7_q, R8_q, R9_q, R10_q, R11_q, R12_q, R13_q, R14_q,
       Tmp_q;

  Decoder #(.enable("false"), .select(4)) decoder_1 (
    .out0(decoder_1_out0), .out1(decoder_1_out1), .out2(decoder_1_out2), .out3(decoder_1_out3),
    .out4(decoder_1_out4), .out5(decoder_1_out5), .out6(decoder_1_out6), .out7(decoder_1_out7),
    .out8(decoder_1_out8), .out9(decoder_1_out9), .out10(decoder_1_out10), .out11(decoder_1_out11),
    .out12(decoder_1_out12), .out13(decoder_1_out13), .out14(decoder_1_out14), .out15(decoder_1_out15),
    .sel(DR));
  Register #(.width(32)) R0 (.D(DRD), .en(and_1_out), .clk(C), .Q(R0_q), .clr(R));
  and and_1 (and_1_out, decoder_1_out0, W);
  Register #(.width(32)) R1 (.D(DRD), .en(and_2_out), .clk(C), .Q(R1_q), .clr(R));
  and and_2 (and_2_out, decoder_1_out1, W);
  Register #(.width(32)) R2 (.D(DRD), .en(and_3_out), .clk(C), .Q(R2_q), .clr(R));
  and and_3 (and_3_out, decoder_1_out2, W);
  and and_4 (and_4_out, decoder_1_out3, W);
  and and_5 (and_5_out, decoder_1_out4, W);
  and and_6 (and_6_out, decoder_1_out5, W);
  Register #(.width(32)) R3 (.D(DRD), .en(and_4_out), .clk(C), .Q(R3_q), .clr(R));
  Register #(.width(32)) R4 (.D(DRD), .en(and_5_out), .clk(C), .Q(R4_q), .clr(R));
  Register #(.width(32)) R5 (.D(DRD), .en(and_6_out), .clk(C), .Q(R5_q), .clr(R));
  Register #(.width(32)) R6 (.D(DRD), .en(and_7_out), .clk(C), .Q(R6_q), .clr(R));
  and and_7 (and_7_out, decoder_1_out6, W);
  Register #(.width(32)) R7 (.D(DRD), .en(and_8_out), .clk(C), .Q(R7_q), .clr(R));
  and and_8 (and_8_out, decoder_1_out7, W);
  Register #(.width(32)) R8 (.D(DRD), .en(and_9_out), .clk(C), .Q(R8_q), .clr(R));
  and and_9 (and_9_out, decoder_1_out8, W);
  Register #(.width(32)) R9 (.D(DRD), .en(and_10_out), .clk(C), .Q(R9_q), .clr(R));
  and and_10 (and_10_out, decoder_1_out9, W);
  Register #(.width(32)) R10 (.D(DRD), .en(and_11_out), .clk(C), .Q(R10_q), .clr(R));
  and and_11 (and_11_out, decoder_1_out10, W);
  and and_12 (and_12_out, decoder_1_out11, W);
  and and_13 (and_13_out, decoder_1_out12, W);
  and and_14 (and_14_out, decoder_1_out13, W);
  Register #(.width(32)) R11 (.D(DRD), .en(and_12_out), .clk(C), .Q(R11_q), .clr(R));
  Register #(.width(32)) R12 (.D(DRD), .en(and_13_out), .clk(C), .Q(R12_q), .clr(R));
  Register #(.width(32)) R13 (.D(DRD), .en(and_14_out), .clk(C), .Q(R13_q), .clr(R));
  Register #(.width(32)) R14 (.D(DRD), .en(and_15_out), .clk(C), .Q(R14_q), .clr(R));
  and and_15 (and_15_out, decoder_1_out14, W);
  Register #(.width(32)) Tmp (.D(DRD), .en(and_16_out), .clk(C), .Q(Tmp_q), .clr(R));
  and and_16 (and_16_out, decoder_1_out15, W);
  Multiplexer #(.select(4), .width(32)) multiplexer_1 (
    .in0(R0_q), .in1(R1_q), .in2(R2_q), .in3(R3_q), .in4(R4_q), .in5(R5_q), .in6(R6_q), .in7(R7_q),
    .in8(R8_q), .in9(R9_q), .in10(R10_q), .in11(R11_q), .in12(R12_q), .in13(R13_q), .in14(R14_q),
    .in15(Tmp_q), .out(S1), .sel(RS1));
  Multiplexer #(.select(4), .width(32)) multiplexer_2 (
    .in0(R0_q), .in1(R1_q), .in2(R2_q), .in3(R3_q), .in4(R4_q), .in5(R5_q), .in6(R6_q), .in7(R7_q),
    .in8(R8_q), .in9(R9_q), .in10(R10_q), .in11(R11_q), .in12(R12_q), .in13(R13_q), .in14(R14_q),
    .in15(Tmp_q), .out(S2), .sel(RS2));

  // Notes on the sheet:
  //   R0
  //   R1
  //   R2
  //   R3
  //   R4
  //   R5
  //   R6
  //   R7
  //   R8\
  //   R9
  //   R10
  //   R11
  //   R12
  //   R13
  //   R14
  //   Tmp/Dump
endmodule

module InstrDecoder (
  input  [31:0] IR,
  input  [2:0] flags,
  output [3:0] ALUOP,
  output [3:0] DR,
  output [3:0] SR2,
  output [3:0] SR1,
  output DDI,
  output OD1I,
  output OD2I,
  output [2:0] ODD,
  output [3:0] OP
);

  wire and_2_out, and_3_out, InstrDecoderCA_1_sr1tdr, not_1_out, not_2_out;

  not not_1 (not_1_out, IR[7]);
  not not_2 (not_2_out, IR[8]);
  and and_1 (DDI, IR[7], not_2_out);
  and and_2 (and_2_out, not_1_out, not_2_out);
  or or_1 (OD1I, and_2_out, and_3_out);
  and and_3 (and_3_out, IR[7], IR[8]);
  InstrDecoderCA InstrDecoderCA_1 (
    .OP(IR[31:28]), .JMPIF(IR[25:24]), .carry(flags[0]), .comp(flags[2]), .POP(OP),
    .SR1TDR(InstrDecoderCA_1_sr1tdr));
  Multiplexer #(.width(4)) multiplexer_1 (.in0(IR[19:16]), .in1(IR[27:24]), .out(DR), .sel(InstrDecoderCA_1_sr1tdr));

  assign ALUOP = IR[15:12];
  assign OD2I = IR[8];
  assign ODD = IR[11:9];
  assign SR1 = IR[27:24];
  assign SR2 = IR[23:20];

  // Other names for the same wires on the sheet: carry = flags[0]; comp = flags[2]
endmodule

module counter_3_bit (
  input  C,
  input  R,
  output [2:0] count
);

  wire j_k_ff_1_qn, j_k_ff_2_qn, j_k_ff_3_qn, not_1_out, not_2_out, not_3_out;

  J_K_Flip_Flop j_k_ff_1 (
    .J(j_k_ff_1_qn), .K(not_1_out), .clk(C), .Q(count[0]), .Qn(j_k_ff_1_qn), .reset(R));  // open: preset
  not not_1 (not_1_out, j_k_ff_1_qn);
  J_K_Flip_Flop j_k_ff_2 (
    .J(j_k_ff_2_qn), .K(not_2_out), .clk(j_k_ff_1_qn), .Q(count[1]), .Qn(j_k_ff_2_qn), .reset(R));  // open: preset
  not not_2 (not_2_out, j_k_ff_2_qn);
  J_K_Flip_Flop j_k_ff_3 (
    .J(j_k_ff_3_qn), .K(not_3_out), .clk(j_k_ff_2_qn), .Q(count[2]), .Qn(j_k_ff_3_qn), .reset(R));  // open: preset
  not not_3 (not_3_out, j_k_ff_3_qn);
endmodule

module InstrDecoderCA (
  input  [3:0] OP,
  input  [1:0] JMPIF,
  input  carry,
  input  comp,
  output [3:0] POP,
  output SR1TDR
);

  wire and_1_out, and_2_out, and_3_out, and_4_out, and_5_out, and_6_out, and_7_out, and_8_out, and_9_out,
       and_10_out, and_11_out, and_12_out, and_13_out, and_14_out, not_1_out, not_2_out, not_3_out,
       not_4_out, not_5_out, not_6_out;

  not not_1 (not_1_out, OP[3]);
  not not_2 (not_2_out, OP[1]);
  not not_3 (not_3_out, OP[0]);
  not not_4 (not_4_out, JMPIF[1]);
  not not_5 (not_5_out, JMPIF[0]);
  not not_6 (not_6_out, comp);
  and and_1 (and_1_out, OP[1], not_3_out);
  and and_2 (and_2_out, OP[1], not_4_out, not_5_out);
  and and_3 (and_3_out, OP[1], not_4_out, carry);
  and and_4 (and_4_out, OP[1], not_5_out, comp);
  and and_5 (and_5_out, OP[1], JMPIF[1], JMPIF[0], not_6_out);
  and and_6 (and_6_out, OP[2], OP[1]);
  and and_7 (and_7_out, OP[3], OP[1]);
  and and_8 (and_8_out, not_2_out, OP[0]);
  and and_9 (and_9_out, OP[0], not_4_out, not_5_out);
  and and_10 (and_10_out, OP[0], not_4_out, carry);
  and and_11 (and_11_out, OP[0], not_5_out, comp);
  and and_12 (and_12_out, OP[0], JMPIF[1], JMPIF[0], not_6_out);
  and and_13 (and_13_out, OP[2], OP[0]);
  and and_14 (and_14_out, OP[3], OP[0]);
  and and_15 (SR1TDR, not_1_out, OP[2], not_3_out);
  or or_1 (POP[1], and_1_out, and_2_out, and_3_out, and_4_out, and_5_out, and_6_out, and_7_out);
  or or_2 (POP[0], and_8_out, and_9_out, and_10_out, and_11_out, and_12_out, and_13_out, and_14_out);

  assign POP[3:2] = OP[3:2];
endmodule

module Executor (
  input  [3:0] OP,
  input  clock,
  input  reset,
  output JMP,
  output PCU,
  output PCO,
  output DRW,
  output SR1O,
  output SR2O,
  output ALUCalc,
  output MI,
  output ML,
  output MO,
  output IRI,
  output IRO,
  output IRAO,
  output ARI,
  output OEn,
  output HLT
);

  wire ExecutorCA_1_jsc1, ExecutorCA_1_rsc, or_1_out;
  wire [2:0] counter_1_q;

  or or_1 (or_1_out, reset, ExecutorCA_1_rsc);
  Counter #(.max('h7), .width(3)) counter_1 (
    .clr(or_1_out), .load(ExecutorCA_1_jsc1), .up(1'b1), .count(1'b1), .clk(clock), .D(3'b001),
    .Q(counter_1_q));  // open: carry
  ExecutorCA ExecutorCA_1 (
    .OP(OP), .SBC(counter_1_q), .JMP(JMP), .PCU(PCU), .PCO(PCO), .DRW(DRW), .SR1O(SR1O), .SR2O(SR2O),
    .ALUCalc(ALUCalc), .MI(MI), .ML(ML), .MO(MO), .IRI(IRI), .IRO(IRO), .IRAO(IRAO), .ARI(ARI), .OEn(OEn),
    .HLT(HLT), .JSC1(ExecutorCA_1_jsc1), .RSC(ExecutorCA_1_rsc));
endmodule

module ExecutorCA (
  input  [3:0] OP,
  input  [2:0] SBC,
  output JMP,
  output PCU,
  output PCO,
  output DRW,
  output SR1O,
  output SR2O,
  output ALUCalc,
  output MI,
  output ML,
  output MO,
  output IRI,
  output IRO,
  output IRAO,
  output ARI,
  output OEn,
  output HLT,
  output JSC1,
  output RSC
);

  wire and_2_out, and_3_out, and_4_out, and_5_out, and_6_out, and_7_out, and_8_out, and_9_out, and_10_out,
       and_11_out, and_12_out, and_13_out, and_14_out, and_15_out, and_16_out, and_17_out, and_18_out,
       and_19_out, and_20_out, and_21_out, and_22_out, and_23_out, and_24_out, and_25_out, and_26_out,
       and_27_out, and_28_out, and_31_out, and_32_out, and_35_out, and_36_out, and_37_out, and_38_out,
       and_39_out, and_40_out, and_41_out, and_42_out, and_43_out, not_1_out, not_2_out, not_3_out,
       not_4_out, not_5_out, not_6_out, not_7_out;

  not not_1 (not_1_out, OP[3]);
  not not_2 (not_2_out, OP[2]);
  not not_3 (not_3_out, OP[1]);
  not not_4 (not_4_out, OP[0]);
  not not_5 (not_5_out, SBC[2]);
  not not_6 (not_6_out, SBC[1]);
  not not_7 (not_7_out, SBC[0]);
  and and_1 (JMP, not_1_out, not_2_out, OP[1], OP[0], not_5_out, SBC[1], SBC[0]);
  and and_2 (and_2_out, not_5_out, not_6_out, SBC[0]);
  and and_3 (and_3_out, not_1_out, not_2_out, OP[1], OP[0], not_5_out, SBC[0]);
  and and_4 (and_4_out, not_5_out, not_6_out, not_7_out);
  and and_5 (and_5_out, not_1_out, OP[2], not_3_out, not_5_out, SBC[1], SBC[0]);
  and and_6 (and_6_out, not_2_out, not_3_out, OP[0], not_5_out, not_7_out);
  and and_7 (and_7_out, not_1_out, OP[1], not_4_out, not_5_out, not_7_out);
  and and_8 (and_8_out, not_2_out, OP[1], not_4_out, not_5_out, not_7_out);
  and and_9 (and_9_out, not_1_out, OP[2], OP[1], not_4_out, not_5_out, SBC[1], not_7_out);
  and and_10 (and_10_out, not_1_out, OP[2], not_3_out, not_5_out, SBC[1], SBC[0]);
  and and_11 (and_11_out, not_2_out, not_3_out, OP[0], not_5_out, SBC[1], not_7_out);
  and and_12 (and_12_out, OP[3], not_2_out, not_4_out, not_5_out, SBC[1], not_7_out);
  and and_13 (and_13_out, not_1_out, OP[2], OP[1], OP[0], not_5_out, SBC[1], not_7_out);
  and and_14 (and_14_out, OP[3], not_2_out, not_3_out, not_5_out, SBC[1], not_7_out);
  and and_15 (and_15_out, OP[3], not_2_out, not_3_out, not_4_out, not_5_out, SBC[1], not_7_out);
  and and_16 (and_16_out, not_1_out, not_2_out, OP[1], OP[0], not_5_out, SBC[1], not_7_out);
  and and_17 (and_17_out, not_1_out, OP[2], not_3_out, OP[0], not_5_out, SBC[1], not_7_out);
  and and_18 (and_18_out, not_1_out, not_2_out, OP[1], not_4_out, not_5_out, SBC[1], not_7_out);
  and and_19 (and_19_out, not_1_out, not_2_out, not_3_out, OP[0], not_5_out, SBC[1], not_7_out);
  and and_20 (and_20_out, OP[3], not_2_out, not_3_out, not_4_out, not_5_out, SBC[1], not_7_out);
  and and_21 (and_21_out, not_1_out, OP[2], OP[1], OP[0], not_5_out, SBC[1], not_7_out);
  and and_22 (and_22_out, not_5_out, not_6_out, not_7_out);
  and and_23 (and_23_out, not_2_out, not_3_out, OP[0], not_5_out, not_7_out);
  and and_24 (and_24_out, not_2_out, OP[1], not_4_out, not_5_out, not_7_out);
  and and_25 (and_25_out, not_1_out, OP[2], not_3_out, not_5_out, SBC[1]);
  and and_26 (and_26_out, not_1_out, OP[2], not_4_out, not_5_out, not_7_out);
  and and_27 (and_27_out, not_5_out, not_6_out, SBC[0]);
  and and_28 (and_28_out, not_1_out, OP[2], not_3_out, not_5_out, SBC[0]);
  and and_29 (IRI, not_5_out, not_6_out, SBC[0]);
  and and_30 (IRO, not_1_out, OP[2], OP[1], not_4_out, not_5_out, SBC[1], not_7_out);
  and and_31 (and_31_out, not_1_out, OP[2], not_3_out, not_4_out, not_5_out, SBC[1], not_7_out);
  and and_32 (and_32_out, not_1_out, OP[2], OP[1], OP[0], not_5_out, SBC[1], not_7_out);
  and and_33 (ARI, not_1_out, not_2_out, OP[1], OP[0], not_5_out, SBC[1], not_7_out);
  and and_34 (OEn, OP[3], not_2_out, OP[1], not_4_out, not_5_out, SBC[1], not_7_out);
  and and_35 (and_35_out, OP[3], OP[2], not_5_out, SBC[1], not_7_out);
  and and_36 (and_36_out, OP[3], OP[1], OP[0], not_5_out, SBC[1], not_7_out);
  and and_37 (and_37_out, not_1_out, OP[1], not_4_out, not_5_out, SBC[1], SBC[0]);
  and and_38 (and_38_out, not_2_out, OP[1], not_4_out, not_5_out, SBC[1], SBC[0]);
  and and_39 (and_39_out, not_1_out, OP[2], not_3_out, SBC[2], not_6_out, not_7_out);
  and and_40 (and_40_out, not_2_out, not_3_out, OP[0], not_5_out, SBC[1], SBC[0]);
  and and_41 (and_41_out, OP[3], not_3_out, not_4_out, not_5_out, SBC[1], SBC[0]);
  and and_42 (and_42_out, OP[3], OP[2], not_5_out, SBC[1], SBC[0]);
  and and_43 (and_43_out, OP[1], OP[0], not_5_out, SBC[1], SBC[0]);
  or or_1 (PCU, and_2_out, and_3_out);
  or or_2 (PCO, and_4_out, and_5_out, and_6_out, and_7_out, and_8_out);
  or or_3 (DRW, and_9_out, and_10_out, and_11_out);
  or or_4 (SR1O, and_12_out, and_13_out, and_14_out);
  or or_5 (SR2O, and_15_out, and_16_out, and_17_out);
  or or_6 (ALUCalc, and_18_out, and_19_out);
  or or_7 (MI, and_20_out, and_21_out);
  or or_8 (ML, and_22_out, and_23_out, and_24_out, and_25_out, and_26_out);
  or or_9 (MO, and_27_out, and_28_out);
  or or_10 (IRAO, and_31_out, and_32_out);
  or or_11 (HLT, and_35_out, and_36_out);
  or or_12 (JSC1, and_37_out, and_38_out, and_39_out, and_40_out);
  or or_13 (RSC, and_41_out, and_42_out, and_43_out);
endmodule

module MemAcces (
  input  [23:0] Adress,
  input  O,
  input  W,
  output ML,
  output MW,
  output ODcodW,
  output OD1W,
  output OD2W,
  output OD3W
);

  wire and_1_out, undriven;
  wire [2:0] undriven_2;

  and and_1 (and_1_out, Adress[23], Adress[22], Adress[21], Adress[20], Adress[19], Adress[18], Adress[17], Adress[16], Adress[15], Adress[14], Adress[13], Adress[12], Adress[11], Adress[10], Adress[9], Adress[8], Adress[7], Adress[6], Adress[5], Adress[4], Adress[3]);
  MemAccesCA MemAccesCA_1 (
    .regOrMem(undriven), .regID(undriven_2), .O(O), .W(W), .ML(ML), .MW(MW), .ODcodW(ODcodW), .OD1W(OD1W),
    .OD2W(OD2W), .OD3W(OD3W));
endmodule

module MemAccesCA (
  input  regOrMem,
  input  [2:0] regID,
  input  O,
  input  W,
  output ML,
  output MW,
  output ODcodW,
  output OD1W,
  output OD2W,
  output OD3W
);

  wire not_1_out, not_2_out, not_3_out, not_4_out;

  not not_1 (not_1_out, regOrMem);
  not not_2 (not_2_out, regID[2]);
  not not_3 (not_3_out, regID[1]);
  not not_4 (not_4_out, regID[0]);
  and and_1 (ML, not_1_out, O);
  and and_2 (MW, not_1_out, W);
  and and_3 (ODcodW, regOrMem, not_2_out, not_3_out, not_4_out, W);
  and and_4 (OD1W, regOrMem, not_2_out, not_3_out, regID[0], W);
  and and_5 (OD2W, regOrMem, not_2_out, regID[1], not_4_out, W);
  and and_6 (OD3W, regOrMem, not_2_out, regID[1], regID[0], W);
endmodule
